# Fritzing sketch BMWCar (saved by Fritzing 0.9.10b)
breadboards: 1

parts:
  J1 = Basic Servo
  M1 = DOIT Esp32 DevKit v1 (30 pins long, 11 pins width) [part_number=ESP32S-PIN30]
  L298N1 = L298N DC motor driver
  U1 = LIPO-1000mAh [package=lipo-1000]
  M2 = DC Motor [voltage_(max)=6V voltage_(min)=3V]

nets:
  GND: J1.gnd, M1.GND, L298N1.GND, U1.-
  VCC: J1.vcc, M1.VIN, L298N1.5V
  N1: J1.pulse, M1.D12
  N2: M1.D32, L298N1.IN1
  N3: M1.D33, L298N1.IN2
  N4: M1.D13, L298N1.ENA
  N5: L298N1.OUT1, M2.pin_2
  N6: L298N1.OUT2, M2.pin_1
  N7: L298N1.12V, U1.+

custom parts:
  DOIT Esp32 DevKit v1 (30 pins long, 11 pins width): The DOIT Esp32 DevKit v1 is one of the development board created by DOIT to evaluate the ESP-WROOM-32 module. It is based on the ESP32 microcontroller that boasts Wifi, Bluetooth, Ethernet and Low Power support all in a single chip. (vanepp) made breadboard work, adjusted pin numbering and labels and reduced size of schematic and cleaned up pcb. This chip is 30pins long (2 x15) and 11 pins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
  L298N DC motor driver: 2x DC motor driver with 78M05 positive voltage regulator (7..35 V) L298N: max 46 V, 2 A Set 5 V Enable jumper to enable 5 V regultor (needed for the L298N) and +5 V output at screw terminal or supply external +5 V at screw terminal Set ENA and/or ENB to +5 V to enable motor permanently or supply ENA and/or ENB with PWM signal IN1 and IN2 set rotation directory for motor A (OUT1/OUT2) IN2 and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
